// Logisim project nibadder.circ as structural Verilog: 1 circuit, main circuit main
module main (
  input  cin,
  input  [3:0] inputA,
  input  [3:0] inputB,
  output [3:0] AplusB,
  output Carry
);

  wire and_1_out, and_2_out, and_3_out, and_4_out, and_5_out, and_6_out, and_7_out, and_8_out, and_9_out,
       and_10_out, and_11_out, and_12_out, or_1_out, or_2_out, or_3_out, or_4_out, Value1_out, Value2_out,
       Value3_out, xor_1_out, xor_2_out, xor_3_out, xor_4_out;

  xor xor_1 (xor_1_out, cin, inputA[0]);
  and and_1 (and_1_out, inputA[0], cin);
  and and_2 (and_2_out, inputB[0], cin);
  and and_3 (and_3_out, inputB[0], inputA[0]);
  xor xor_2 (xor_2_out, Value1_out, inputA[1]);
  and and_4 (and_4_out, inputA[1], Value1_out);
  and and_5 (and_5_out, inputB[1], Value1_out);
  and and_6 (and_6_out, inputB[1], inputA[1]);
  xor xor_3 (xor_3_out, Value2_out, inputA[2]);
  and and_7 (and_7_out, inputA[2], Value2_out);
  and and_8 (and_8_out, inputB[2], Value2_out);
  and and_9 (and_9_out, inputB[2], inputA[2]);
  xor xor_4 (xor_4_out, Value3_out, inputA[3]);
  and and_10 (and_10_out, inputA[3], Value3_out);
  and and_11 (and_11_out, inputB[3], Value3_out);
  and and_12 (and_12_out, inputB[3], inputA[3]);
  or or_1 (or_1_out, and_1_out, and_2_out);
  xor Bit2 (AplusB[1], xor_2_out, inputB[1]);
  or or_2 (or_2_out, and_4_out, and_5_out);
  or or_3 (or_3_out, and_7_out, and_8_out);
  xor Bit4 (AplusB[3], xor_4_out, inputB[3]);
  or or_4 (or_4_out, and_10_out, and_11_out);
  xor Bit1 (AplusB[0], xor_1_out, inputB[0]);
  or Value2 (Value2_out, or_2_out, and_6_out);
  xor Bit3 (AplusB[2], xor_3_out, inputB[2]);
  or Value3 (Value3_out, or_3_out, and_9_out);
  or Value1 (Value1_out, or_1_out, and_3_out);
  or Value4 (Carry, or_4_out, and_12_out);
endmodule
