// Logisim project Registerfile.circ as structural Verilog: 1 circuit, main circuit main
module main (
  input  [1:0] WriteReg,
  input  [1:0] ReadReg1,
  input  [1:0] ReadReg2,
  input  [7:0] RegDataW,
  input  RegWrite,
  output [7:0] RegData1,
  output [7:0] RegData2
);

  wire and_1_out, and_2_out, and_3_out, and_4_out, clock_1_out, decoder_1_out0, decoder_1_out1,
       decoder_1_out2, decoder_1_out3;
  wire [7:0] register_1_q, register_2_q, register_3_q, register_4_q;

  Clock clock_1 (.out(clock_1_out));
  Decoder #(.select(2)) decoder_1 (
    .out0(decoder_1_out0), .out1(decoder_1_out1), .out2(decoder_1_out2), .out3(decoder_1_out3), .sel(WriteReg));  // open: en
  and and_1 (and_1_out, decoder_1_out1, RegWrite);
  and and_2 (and_2_out, decoder_1_out2, RegWrite);
  Register register_1 (.D(RegDataW), .en(and_3_out), .clk(clock_1_out), .Q(register_1_q));  // open: clr
  and and_3 (and_3_out, decoder_1_out0, RegWrite);
  Register register_2 (.D(RegDataW), .en(and_1_out), .clk(clock_1_out), .Q(register_2_q));  // open: clr
  Register register_3 (.D(RegDataW), .en(and_2_out), .clk(clock_1_out), .Q(register_3_q));  // open: clr
  Register register_4 (.D(RegDataW), .en(and_4_out), .clk(clock_1_out), .Q(register_4_q));  // open: clr
  and and_4 (and_4_out, decoder_1_out3, RegWrite);
  Multiplexer #(.select(2), .width(8)) multiplexer_1 (
    .in0(register_1_q), .in1(register_2_q), .in2(register_3_q), .in3(register_4_q), .out(RegData1),
    .sel(ReadReg1));
  Multiplexer #(.select(2), .width(8)) multiplexer_2 (
    .in0(register_1_q), .in1(register_2_q), .in2(register_3_q), .in3(register_4_q), .out(RegData2),
    .sel(ReadReg2));

  // Notes on the sheet:
  //   Michael Buzzetta
  //   I pledge my honor that I have abided by the stevens honor system
endmodule
