// Logisim project CPU_cirucit.circ as structural Verilog: 2 circuits, main circuit main
module main (
  output [31:0] out_1
);

  wire Clock1_out, undriven;
  wire [1:0] multiplexer_1_out;
  wire [3:0] multiplexer_2_out, multiplexer_2_out_2, registerfile_1_x0, registerfile_1_x0_2,
       registerfile_1_x1, registerfile_1_x1_2;
  wire [7:0] adder_1_out, adder_2_out, divider_1_out, multiplexer_3_out, multiplexer_4_out, multiplier_1_out,
       ram_1_dout, register_1_q, registerfile_1_regdata1, registerfile_1_regdata2, registerfile_1_x2,
       registerfile_1_x3, subtractor_1_out;

  Clock Clock1 (.out(Clock1_out));
  Register register_1 (.D(adder_1_out), .clk(Clock1_out), .Q(register_1_q));  // open: en, clr
  Hex_Digit_Display #(.decimalPoint("false")) ALUOUT (.value(multiplexer_2_out_2));
  Hex_Digit_Display #(.decimalPoint("false")) hex_digit_display_1 (.value(multiplexer_2_out));
  Adder adder_1 (.a(register_1_q), .b(8'h1), .out(adder_1_out));  // open: cin, cout
  Multiplexer #(.width(2)) multiplexer_1 (
    .in0(out_1[3:2]), .in1({out_1[4], out_1[5]}), .out(multiplexer_1_out), .sel(undriven));
  Hex_Digit_Display #(.decimalPoint("false")) X0 (.value(registerfile_1_x0_2));
  Multiplexer #(.width(8)) multiplexer_2 (
    .in0(multiplexer_4_out), .in1(ram_1_dout), .out({multiplexer_2_out_2, multiplexer_2_out}), .sel(out_1[12]));
  Hex_Digit_Display #(.decimalPoint("false")) hex_digit_display_2 (.value(registerfile_1_x0));
  Hex_Digit_Display #(.decimalPoint("false")) X1 (.value(registerfile_1_x1_2));
  RegisterFile registerfile_1 (
    .Clock(Clock1_out), .WriteReg(out_1[3:2]), .ReadReg1(out_1[1:0]), .ReadReg2(multiplexer_1_out),
    .RegDataW({multiplexer_2_out_2, multiplexer_2_out}), .RegWrite(out_1[8]),
    .RegData1(registerfile_1_regdata1), .RegData2(registerfile_1_regdata2),
    .X0({registerfile_1_x0_2, registerfile_1_x0}), .X1({registerfile_1_x1_2, registerfile_1_x1}),
    .X2(registerfile_1_x2), .X3(registerfile_1_x3));
  Hex_Digit_Display #(.decimalPoint("false")) hex_digit_display_3 (.value(registerfile_1_x1));
  Hex_Digit_Display #(.decimalPoint("false")) X2 (.value(registerfile_1_x2[7:4]));
  Hex_Digit_Display #(.decimalPoint("false")) hex_digit_display_4 (.value(registerfile_1_x2[3:0]));
  Multiplexer #(.width(8)) multiplexer_3 (
    .in0(registerfile_1_regdata2), .in1({{5{out_1[7]}}, out_1[6:4]}), .out(multiplexer_3_out), .sel(out_1[11]));
  Hex_Digit_Display #(.decimalPoint("false")) X3 (.value(registerfile_1_x3[7:4]));
  Hex_Digit_Display #(.decimalPoint("false")) hex_digit_display_5 (.value(registerfile_1_x3[3:0]));
  ROM #(.dataWidth(32)) rom_1 (.addr(adder_1_out), .data(out_1));
  Multiplier multiplier_1 (
    .a(registerfile_1_regdata1), .b(multiplexer_3_out), .out(multiplier_1_out));  // open: cin, cout
  Divider divider_1 (.a(registerfile_1_regdata1), .b(multiplexer_3_out), .out(divider_1_out));  // open: upper, rem
  Subtractor subtractor_1 (
    .a(registerfile_1_regdata1), .b(multiplexer_3_out), .out(subtractor_1_out));  // open: bin, bout
  Adder adder_2 (.a(registerfile_1_regdata1), .b(multiplexer_3_out), .out(adder_2_out));  // open: cin, cout
  RAM ram_1 (
    .addr(multiplexer_4_out), .we(out_1[14]), .oe(out_1[13]), .clk(Clock1_out),
    .din(registerfile_1_regdata2), .dout(ram_1_dout));
  Multiplexer #(.select(2), .width(8)) multiplexer_4 (
    .in0(multiplier_1_out), .in1(subtractor_1_out), .in2(divider_1_out), .in3(adder_2_out),
    .out(multiplexer_4_out), .sel(out_1[10:9]));

  // Notes on the sheet:
  //   RegDataW
  //   I hereby name this CPU, Sixtus
  //   contents of rom_1 (hex, n*v repeats v):
  //   a30303a 20316630 36203166 30392031 66306620 33623134 20336232 38203362 33632033 66303520 33663061
  //   20336630 66203662 30612036 66303620 35373064 20343730 65203030 30302030 30303020 30303030 a31303a
  //   20303030 30203030 30302030 30303020 30303030 20303030 30203030 30302030 30303020 30303030 20303030
  //   30203030 30302030 30303020 30303030 20303030 30203030 30302030 30303020 30303030 a32303a 20303030
  //   30203030 30302030 30303020 30303030 20303030 30203030 30302030 30303020 30303030 20303030 30203030
  //   30302030 30303020 30303030 20303030 30203030 30302030 30303020 30303030 a33303a 20303030 30203030
  //   30302030 30303020 30303030 20303030 30203030 30302030 30303020 30303030 20303030 30203030 30302030
  //   30303020 30303030 20303030 30203030 30302030 30303020 30303030 a34303a 20303030 30203030 30302030
  //   30303020 30303030 20303030 30203030 30302030 30303020 30303030 20303030 30203030 30302030 30303020
  //   30303030 20303030 30203030 30302030 30303020 30303030 a35303a 20303030 30203030 30302030 30303020
  //   30303030 20303030 30203030 30302030 30303020 30303030 20303030 30203030 30302030 30303020 30303030
  //   20303030 30203030 30302030 30303020 30303030 a36303a 20303030 30203030 30302030 30303020 30303030
  //   20303030 30203030 30302030 30303020 30303030 20303030 30203030 30302030 30303020 30303030 20303030
  //   30203030 30302030 30303020 30303030 a37303a 20303030 30203030 30302030 30303020 30303030 20303030
  //   30203030 30302030 30303020 30303030 20303030 30203030 30302030 30303020 30303030 20303030 30203030
  //   30302030 30303020 30303030 a38303a 20303030 30203030 30302030 30303020 30303030 20303030 30203030
  //   30302030 30303020 30303030 20303030 30203030 30302030 30303020 30303030 20303030 30203030 30302030
  //   30303020 30303030 a39303a 20303030 30203030 30302030 30303020 30303030 20303030 30203030 30302030
  //   30303020 30303030 20303030 30203030 30302030 30303020 30303030 20303030 30203030 30302030 30303020
  //   30303030 a61303a 20303030 30203030 30302030 30303020 30303030 20303030 30203030 30302030 30303020
  //   30303030 20303030 30203030 30302030 30303020 30303030 20303030 30203030 30302030 30303020 30303030
  //   a62303a 20303030 30203030 30302030 30303020 30303030 20303030 30203030 30302030 30303020 30303030
  //   20303030 30203030 30302030 30303020 30303030 20303030 30203030 30302030 30303020 30303030 a63303a
  //   20303030 30203030 30302030
  //   Michael Buzzetta Owen Krupa
  //   I pledge my honor that I have abided by the Stevens Honor System
endmodule

module RegisterFile (
  input  Clock,
  input  [1:0] WriteReg,
  input  [1:0] ReadReg1,
  input  [1:0] ReadReg2,
  input  [7:0] RegDataW,
  input  RegWrite,
  output [7:0] RegData1,
  output [7:0] RegData2,
  output [7:0] X0,
  output [7:0] X1,
  output [7:0] X2,
  output [7:0] X3
);

  wire and_1_out, and_2_out, and_3_out, and_4_out, decoder_1_out0, decoder_1_out1, decoder_1_out2,
       decoder_1_out3;

  Decoder #(.select(2)) decoder_1 (
    .out0(decoder_1_out0), .out1(decoder_1_out1), .out2(decoder_1_out2), .out3(decoder_1_out3), .sel(WriteReg));  // open: en
  and and_1 (and_1_out, decoder_1_out1, RegWrite);
  and and_2 (and_2_out, decoder_1_out2, RegWrite);
  Register register_1 (.D(RegDataW), .en(and_3_out), .clk(Clock), .Q(X0));  // open: clr
  and and_3 (and_3_out, decoder_1_out0, RegWrite);
  Register register_2 (.D(RegDataW), .en(and_1_out), .clk(Clock), .Q(X1));  // open: clr
  Register register_3 (.D(RegDataW), .en(and_2_out), .clk(Clock), .Q(X2));  // open: clr
  Register register_4 (.D(RegDataW), .en(and_4_out), .clk(Clock), .Q(X3));  // open: clr
  and and_4 (and_4_out, decoder_1_out3, RegWrite);
  Multiplexer #(.select(2), .width(8)) multiplexer_1 (
    .in0(X0), .in1(X1), .in2(X2), .in3(X3), .out(RegData1), .sel(ReadReg1));
  Multiplexer #(.select(2), .width(8)) multiplexer_2 (
    .in0(X0), .in1(X1), .in2(X2), .in3(X3), .out(RegData2), .sel(ReadReg2));
endmodule
