// Logisim project LeastReqsComputer.circ as structural Verilog: 10 circuits, main circuit main
module main (
);

  wire clock_1_out, instdec_1_alusrc, instdec_1_memread, instdec_1_memtoreg, instdec_1_memwrite,
       instdec_1_reg2loc, instdec_1_regwrite;
  wire [1:0] alucontrol_1_action, instdec_1_aluop, instdec_1_rd, instdec_1_rm, instdec_1_rn, instdec_1_rt,
       multiplexer_1_out;
  wire [7:0] alu_1_aluout, datamemory_1_readdatam, instdec_1_imm, instdec_1_opcode, pc_1_pcout,
       pcadder_1_nextrpc, regfile_1_regdata1, regfile_1_regdata2, writebackmux_1_regdataw;
  wire [19:0] instructionmemory_1_instruction;

  PCAdder pcadder_1 (.PC(pc_1_pcout), .NextrPC(pcadder_1_nextrpc));
  InstDec instdec_1 (
    .Instruction(instructionmemory_1_instruction), .Rm(instdec_1_rm), .imm(instdec_1_imm), .Rn(instdec_1_rn),
    .Rt(instdec_1_rt), .Rd(instdec_1_rd), .Reg2Loc(instdec_1_reg2loc), .ALUsrc(instdec_1_alusrc),
    .MemWrite(instdec_1_memwrite), .MemRead(instdec_1_memread), .MemToReg(instdec_1_memtoreg),
    .RegWrite(instdec_1_regwrite), .Opcode(instdec_1_opcode), .ALUop(instdec_1_aluop));
  Multiplexer #(.width(2)) multiplexer_1 (
    .in0(instdec_1_rt), .in1(instdec_1_rm), .out(multiplexer_1_out), .sel(instdec_1_reg2loc));
  PC pc_1 (.NextPC(pcadder_1_nextrpc), .Clock(clock_1_out), .PCout(pc_1_pcout));
  InstructionMemory instructionmemory_1 (
    .Clock(clock_1_out), .PC(pc_1_pcout), .Instruction(instructionmemory_1_instruction));
  RegFile regfile_1 (
    .Clock(clock_1_out), .ReadReg1(instdec_1_rn), .ReadReg2(multiplexer_1_out), .WriteReg(instdec_1_rd),
    .RegWrite(instdec_1_regwrite), .RegDataW(writebackmux_1_regdataw), .RegData2(regfile_1_regdata2),
    .RegData1(regfile_1_regdata1));
  ALU alu_1 (
    .ALUsrc(instdec_1_alusrc), .Imm(instdec_1_imm), .RegData2(regfile_1_regdata2), .A(regfile_1_regdata1),
    .action(alucontrol_1_action), .ALUout(alu_1_aluout));
  DataMemory datamemory_1 (
    .Clock(clock_1_out), .MemRead(instdec_1_memread), .WriteDataM(regfile_1_regdata2),
    .MemWrite(instdec_1_memwrite), .Address(alu_1_aluout), .ReadDataM(datamemory_1_readdatam));
  WriteBackMUX writebackmux_1 (
    .ALUout(alu_1_aluout), .ReadDataM(datamemory_1_readdatam), .MemToReg(instdec_1_memtoreg),
    .RegDataW(writebackmux_1_regdataw));
  ALUControl alucontrol_1 (.ALUop(instdec_1_aluop), .Opcode(instdec_1_opcode), .action(alucontrol_1_action));
  Clock clock_1 (.out(clock_1_out));

  // Notes on the sheet:
  //   RegWrite
  //   ALUsrc
  //   MemRead
  //   MemWrite
  //   Reg2Loc
  //   MemToReg
  //   ALUop
  //   RegData2
  //   ALUout
  //   RegDataW
endmodule

module PC (
  input  [7:0] NextPC,
  input  Clock,
  output [7:0] PCout
);

  Register register_1 (.D(NextPC), .en(1'b1), .clk(Clock), .Q(PCout));  // open: clr
endmodule

module InstructionMemory (
  input  [7:0] PC,
  input  Clock,
  output [19:0] Instruction
);

  wire not_1_out;

  not not_1 (not_1_out, 1'b0);
  RAM #(.asyncread("true"), .dataWidth(20)) ram_1 (
    .addr(PC), .we(1'b0), .oe(not_1_out), .clk(Clock), .dout(Instruction));  // open: din

  // Notes on the sheet:
  //   MOVimm X0, 0x12 = 82012
  //   MOVR X1, X0 = 81400
  //   MOVimm X1, 0x8 = 82408
  //   MOVimm X3, 0x5 = 82c05
  //   ADDR X2, X1, X0 = 85900
  //   MULR X2, X1, X0 = 89900
  //   SUBR X2, X1, X0 = 8d900
  //   ADDimm X2, X1, 1 = 86901
  //   SUBimm X2, X1, 1 = 8e901
  //   MULimm X2, X1, 2 = 8a902
  //   STR X1 [X0] = 0x16400
  //   LDR X3 [X0] = 0xe6c00
endmodule

module PCAdder (
  input  [7:0] PC,
  output [7:0] NextrPC
);

  Adder adder_1 (.a(PC), .b(8'h1), .out(NextrPC));  // open: cin, cout
endmodule

module InstDec (
  input  [19:0] Instruction,
  output [1:0] Rm,
  output [7:0] imm,
  output [1:0] Rn,
  output [1:0] Rt,
  output [1:0] Rd,
  output [7:0] Opcode,
  output Reg2Loc,
  output ALUsrc,
  output [1:0] ALUop,
  output MemWrite,
  output MemRead,
  output MemToReg,
  output RegWrite
);


  assign ALUop = Instruction[15:14];
  assign ALUsrc = Instruction[13];
  assign imm = Instruction[7:0];
  assign MemRead = Instruction[17];
  assign MemToReg = Instruction[18];
  assign MemWrite = Instruction[16];
  assign Opcode = Instruction[19:12];
  assign Rd = Instruction[11:10];
  assign Reg2Loc = Instruction[12];
  assign RegWrite = Instruction[19];
  assign Rm = Instruction[1:0];
  assign Rn = Instruction[9:8];
  assign Rt = Instruction[11:10];

  // Notes on the sheet:
  //   ALUop/ 00 is passb. 01 is +, 10 is x, 11 is -
  //   MOV X0, 3 = 0x4803
  //   MOV X1, 2 = 0x4882
  //   ADD X0, X0, X1 = 0x6008
  //   LDR X2, [X1]
  //   Opcodes
  //   MOVR: 10000001 = 0x81
  //   MOVimm: 10000010 = 0x82
  //   ADDR: 10000101 = 0x85
  //   ADDImm: 10000110 = 0x86
  //   SUBR: 10001101 = 0x8d
  //   SUBimm: 10001110 = 0x8e
  //   MULR: 10001001 = 0x89
  //   MULimm: 10001010 = 0x8A
  //   STR X0 [X1, 0] = 
  //   LDRImm: 11100110 = 0xe6
  //   STRimm: 00010110 = 0x16
  //   LDRR: e5
  //   STRR: does not exist
  //   MOVimm X0, 0x12 = 82012
  //   MOVR X1, X0 = 81400
  //   MOVimm X1, 0x8 = 82408
  //   ADDR X2, X1, X0 = 85900
  //   MULR X2, X1, X0 = 89900
  //   SUBR X2, X1, X0 = 8d900
  //   ADDimm X2, X1, 1 = 86901
  //   SUBimm X2, X1, 1 = 8e901
  //   MULimm X2, X1, 2 = 8a902
  //   STR X1 [X0] = 0x16400
  //   LDR X3 [X0] = 0xe6c00
  //   10000110111000010100
endmodule

module RegFile (
  input  Clock,
  input  [1:0] ReadReg1,
  input  [1:0] ReadReg2,
  input  RegWrite,
  input  [1:0] WriteReg,
  input  [7:0] RegDataW,
  output [7:0] RegData1,
  output [7:0] RegData2
);

  wire and_1_out, and_2_out, and_3_out, and_4_out, decoder_1_out0, decoder_1_out1, decoder_1_out2,
       decoder_1_out3;
  wire [7:0] X0_q, X1_q, X2_q, X3_q;

  Decoder #(.enable("false"), .select(2)) decoder_1 (
    .out0(decoder_1_out0), .out1(decoder_1_out1), .out2(decoder_1_out2), .out3(decoder_1_out3), .sel(WriteReg));
  Register X0 (.D(RegDataW), .en(and_1_out), .clk(Clock), .Q(X0_q));  // open: clr
  and and_1 (and_1_out, RegWrite, decoder_1_out0);
  Register X1 (.D(RegDataW), .en(and_2_out), .clk(Clock), .Q(X1_q));  // open: clr
  and and_2 (and_2_out, RegWrite, decoder_1_out1);
  Register X2 (.D(RegDataW), .en(and_3_out), .clk(Clock), .Q(X2_q));  // open: clr
  and and_3 (and_3_out, RegWrite, decoder_1_out2);
  Register X3 (.D(RegDataW), .en(and_4_out), .clk(Clock), .Q(X3_q));  // open: clr
  and and_4 (and_4_out, RegWrite, decoder_1_out3);
  Multiplexer #(.select(2), .width(8)) multiplexer_1 (
    .in0(X0_q), .in1(X1_q), .in2(X2_q), .in3(X3_q), .out(RegData1), .sel(ReadReg1));
  Multiplexer #(.select(2), .width(8)) multiplexer_2 (
    .in0(X0_q), .in1(X1_q), .in2(X2_q), .in3(X3_q), .out(RegData2), .sel(ReadReg2));

  // Notes on the sheet:
  //   Kian Holden. I pledge my honor that I have abided by the Stevens Honor System.
endmodule

module ALUControl (
  input  [7:0] Opcode,
  input  [1:0] ALUop,
  output [1:0] action
);


  assign action = ALUop;

  // Notes on the sheet:
  //   0 is +
  //   1 is x
  //   00 is PassB
  //   01 is A+B
  //   10 is AxB
  //   11 is A-B
endmodule

module ALU (
  input  [7:0] RegData2,
  input  [7:0] Imm,
  input  ALUsrc,
  input  [7:0] A,
  input  [1:0] action,
  output [7:0] ALUout
);

  wire [7:0] adder_1_out, bit_extender_1_out, multiplexer_1_out, multiplier_1_out, subtractor_1_out;

  Bit_Extender #(.out_width(8)) bit_extender_1 (.in(Imm), .out(bit_extender_1_out));
  Multiplexer #(.width(8)) multiplexer_1 (
    .in0(RegData2), .in1(bit_extender_1_out), .out(multiplexer_1_out), .sel(ALUsrc));
  Adder adder_1 (.a(multiplexer_1_out), .b(A), .out(adder_1_out));  // open: cin, cout
  Multiplier multiplier_1 (.a(multiplexer_1_out), .b(A), .out(multiplier_1_out));  // open: cin, cout
  Subtractor subtractor_1 (.a(A), .b(multiplexer_1_out), .out(subtractor_1_out));  // open: bin, bout
  Multiplexer #(.select(2), .width(8)) multiplexer_2 (
    .in0(multiplexer_1_out), .in1(adder_1_out), .in2(multiplier_1_out), .in3(subtractor_1_out), .out(ALUout),
    .sel(action));

  // Notes on the sheet:
  //   B
endmodule

module DataMemory (
  input  [7:0] Address,
  input  MemWrite,
  input  MemRead,
  input  Clock,
  input  [7:0] WriteDataM,
  output [7:0] ReadDataM
);

  RAM #(.asyncread("true")) ram_1 (
    .addr(Address), .we(MemWrite), .oe(MemRead), .clk(Clock), .din(WriteDataM), .dout(ReadDataM));
endmodule

module WriteBackMUX (
  input  [7:0] ALUout,
  input  [7:0] ReadDataM,
  input  MemToReg,
  output [7:0] RegDataW
);

  Multiplexer #(.width(8)) multiplexer_1 (.in0(ALUout), .in1(ReadDataM), .out(RegDataW), .sel(MemToReg));
endmodule
